// Logisim project Bull and Cow.circ as structural Verilog: 7 circuits, main circuit block
// 6
module MAIN (
);

  wire _0, _0s, _1, _1p, _1s, _2, _2p, _2s, _3, _3p, _3s, _4, _4p, _4s, _5, _5p, _5s, _6, _6p, _6s, _7, _7p,
       _7s, _8, _8p, _8s, _9, _9p, _9s, _10p, blk, comparator_1_eq, comparator_3_eq, cpu_core_1_clk, en,
       input_io_1_ok_2, \new , nv, ok, rd_rw, win;
  wire [1:0] multiplexer_33_out, multiplexer_34_out, sel;
  wire [3:0] _1_h_1ch, _1_h_1t, _1_h_2ch, _1_h_2t, _1_h_3ch, _1_h_4ch, _1_h_b, _1_h_c, _1tries_tek, _2_h_1ch,
       _2_h_1t, _2_h_2ch, _2_h_2t, _2_h_3ch, _2_h_4ch, _2_h_b, _2_h_c, _2tries_tek, _3_h_1ch, _3_h_1t,
       _3_h_2ch, _3_h_2t, _3_h_3ch, _3_h_4ch, _3_h_b, _3_h_c, _4_h_1ch, _4_h_1t, _4_h_2ch, _4_h_2t, _4_h_3ch,
       _4_h_4ch, _4_h_b, _4_h_c, _5_h_1ch, _5_h_1t, _5_h_2ch, _5_h_2t, _5_h_3ch, _5_h_4ch, _5_h_b, _5_h_c,
       _6_h_1ch, _6_h_1t, _6_h_2ch, _6_h_2t, _6_h_3ch, _6_h_4ch, _6_h_b, _6_h_c, _7_h_1ch, _7_h_1t, _7_h_2ch,
       _7_h_2t, _7_h_3ch, _7_h_4ch, _7_h_b, _7_h_c, _8_h_1ch, _8_h_1t, _8_h_2ch, _8_h_2t, _8_h_3ch, _8_h_4ch,
       _8_h_b, _8_h_c, _9_h_1ch, _9_h_1t, _9_h_2ch, _9_h_2t, _9_h_3ch, _9_h_4ch, _9_h_b, _9_h_c, _10_h_1ch,
       _10_h_1t, _10_h_2ch, _10_h_2t, _10_h_3ch, _10_h_4ch, _10_h_b, _10_h_c, buill_tek, counter_1_q,
       cow_tek, register_1_q, register_2_q, register_3_q, register_4_q, register_5_q, register_6_q,
       register_7_q, register_8_q, register_9_q, register_10_q, register_11_q, register_12_q, register_13_q,
       register_14_q, register_15_q, register_16_q, register_17_q, register_18_q, register_19_q,
       register_20_q, register_21_q, register_22_q, register_23_q, register_24_q, register_25_q,
       register_26_q, register_27_q, register_28_q, register_29_q, register_30_q, register_36_q,
       register_37_q, register_38_q, register_39_q, register_40_q, register_41_q, register_42_q,
       register_43_q, register_44_q, register_45_q, register_46_q, register_47_q, register_48_q,
       register_49_q, register_50_q, register_53_q, register_54_q, register_55_q, register_56_q,
       register_57_q, register_58_q, register_59_q, register_60_q, register_61_q, register_62_q,
       register_63_q, register_64_q, register_65_q;
  wire [7:0] _1d, _1f, _2d, _2f, _3d, _3f, _4d, _4f, _5d, _6d, _7d, _8d, _9d, _10d, _11d, _12d, _13d, _14d,
       _15d, _16d, _17d, _18d, _19d, _20d, _21d, _22d, _23d, _24d, _25d, _26d, _27d, _28d, _29d, _30d, _31d,
       _32d, addr, att_sel, cpu_core_1_addr_in, cpu_core_1_data_out, input_io_1_data_gen_code,
       input_io_1_data_in, register_31_q, register_32_q, register_33_q, register_34_q, register_35_q,
       register_66_q, register_67_q, register_68_q, register_69_q, register_70_q;
  wire [7:4] bullsout, cowsout, register_51_q, register_52_q;

  Hex_Digit_Display hex_digit_display_1 (.value(_1f[3:0]));  // open: dp
  Hex_Digit_Display hex_digit_display_2 (.value(_2f[3:0]));  // open: dp
  Register register_1 (.D(_1f), .en(_1p), .Q({register_1_q, _1_h_1ch}), .clk(en), .clr(\new ));
  Register register_2 (.D(_1f), .en(_2p), .Q({register_2_q, _2_h_1ch}), .clk(en), .clr(\new ));
  Register register_3 (.D(_1f), .en(_3p), .Q({register_3_q, _3_h_1ch}), .clk(en), .clr(\new ));
  Register register_4 (.D(_1f), .en(_4p), .Q({register_4_q, _4_h_1ch}), .clk(en), .clr(\new ));
  Register register_5 (.D(_1f), .en(_5p), .Q({register_5_q, _5_h_1ch}), .clk(en), .clr(\new ));
  Hex_Digit_Display hex_digit_display_3 (.value(_3f[3:0]));  // open: dp
  Hex_Digit_Display hex_digit_display_4 (.value(_4f[3:0]));  // open: dp
  Register register_6 (.D(_2f), .en(_1p), .Q({register_6_q, _1_h_2ch}), .clk(en), .clr(\new ));
  Register register_7 (.D(_2f), .en(_2p), .Q({register_7_q, _2_h_2ch}), .clk(en), .clr(\new ));
  Register register_8 (.D(_2f), .en(_3p), .Q({register_8_q, _3_h_2ch}), .clk(en), .clr(\new ));
  Register register_9 (.D(_2f), .en(_4p), .Q({register_9_q, _4_h_2ch}), .clk(en), .clr(\new ));
  Register register_10 (.D(_2f), .en(_5p), .Q({register_10_q, _5_h_2ch}), .clk(en), .clr(\new ));
  Button u__2 (.out(_2s));
  Button u__1 (.out(_1s));
  Button u__5 (.out(_5s));
  Button u__4 (.out(_4s));
  Button u__7 (.out(_7s));
  Button u__8 (.out(_8s));
  Button u_Nv (.out(nv));
  Button u__0 (.out(_0s));
  Register register_11 (.D(_4f), .en(_1p), .Q({register_11_q, _1_h_4ch}), .clk(en), .clr(\new ));
  Register register_12 (.D(_3f), .en(_1p), .Q({register_12_q, _1_h_3ch}), .clk(en), .clr(\new ));
  Register register_13 (.D(_4f), .en(_2p), .Q({register_13_q, _2_h_4ch}), .clk(en), .clr(\new ));
  Register register_14 (.D(_3f), .en(_2p), .Q({register_14_q, _2_h_3ch}), .clk(en), .clr(\new ));
  Register register_15 (.D(_3f), .en(_3p), .Q({register_15_q, _3_h_3ch}), .clk(en), .clr(\new ));
  Register register_16 (.D(_3f), .en(_4p), .Q({register_16_q, _4_h_3ch}), .clk(en), .clr(\new ));
  Register register_17 (.D(_3f), .en(_5p), .Q({register_17_q, _5_h_3ch}), .clk(en), .clr(\new ));
  Register register_18 (.D(_4f), .en(_5p), .Q({register_18_q, _5_h_4ch}), .clk(en), .clr(\new ));
  Hex_Digit_Display hex_digit_display_5 (.value(buill_tek));  // open: dp
  Button u__3 (.out(_3s));
  Button u__6 (.out(_6s));
  Button u__9 (.out(_9s));
  Button u_ok (.out(ok));
  Register register_19 (.D(_4f), .en(_3p), .Q({register_19_q, _3_h_4ch}), .clk(en), .clr(\new ));
  Register register_20 (.D(_4f), .en(_4p), .Q({register_20_q, _4_h_4ch}), .clk(en), .clr(\new ));
  Hex_Digit_Display hex_digit_display_6 (.value(cow_tek));  // open: dp
  DotMatrix #(.matrixcols(32), .matrixrows(8)) dotmatrix_1 (
    .col0(_1d), .col1(_2d), .col2(_3d), .col3(_4d), .col4(_5d), .col5(_6d), .col6(_7d), .col7(_8d),
    .col8(_9d), .col9(_10d), .col10(_11d), .col11(_12d), .col12(_13d), .col13(_14d), .col14(_15d),
    .col15(_16d), .col16(_17d), .col17(_18d), .col18(_19d), .col19(_20d), .col20(_21d), .col21(_22d),
    .col22(_23d), .col23(_24d), .col24(_25d), .col25(_26d), .col26(_27d), .col27(_28d), .col28(_29d),
    .col29(_30d), .col30(_31d), .col31(_32d));
  Register register_21 (.D({bullsout, buill_tek}), .en(_1p), .Q({register_21_q, _1_h_b}), .clk(en), .clr(\new ));
  Register register_22 (.D({bullsout, buill_tek}), .en(_2p), .Q({register_22_q, _2_h_b}), .clk(en), .clr(\new ));
  Register register_23 (.D({bullsout, buill_tek}), .en(_3p), .Q({register_23_q, _3_h_b}), .clk(en), .clr(\new ));
  Register register_24 (.D({bullsout, buill_tek}), .en(_4p), .Q({register_24_q, _4_h_b}), .clk(en), .clr(\new ));
  Register register_25 (.D({bullsout, buill_tek}), .en(_5p), .Q({register_25_q, _5_h_b}), .clk(en), .clr(\new ));
  Hex_Digit_Display hex_digit_display_7 (.value(_1tries_tek));  // open: dp
  Hex_Digit_Display hex_digit_display_8 (.value(_2tries_tek));  // open: dp
  Button button_1 (.out(\new ));
  Register register_26 (.D({cowsout, cow_tek}), .en(_1p), .Q({register_26_q, _1_h_c}), .clk(en), .clr(\new ));
  Register register_27 (.D({cowsout, cow_tek}), .en(_2p), .Q({register_27_q, _2_h_c}), .clk(en), .clr(\new ));
  Register register_28 (.D({cowsout, cow_tek}), .en(_3p), .Q({register_28_q, _3_h_c}), .clk(en), .clr(\new ));
  Register register_29 (.D({cowsout, cow_tek}), .en(_4p), .Q({register_29_q, _4_h_c}), .clk(en), .clr(\new ));
  Register register_30 (.D({cowsout, cow_tek}), .en(_5p), .Q({register_30_q, _5_h_c}), .clk(en), .clr(\new ));
  bcd bcd_1 (.attempt_2({_1_h_1t, _1_h_2t}), .attempt(register_31_q));
  Register register_31 (.D(att_sel), .en(_1p), .Q(register_31_q), .clk(en), .clr(\new ));
  bcd bcd_2 (.attempt_2({_2_h_1t, _2_h_2t}), .attempt(register_32_q));
  Register register_32 (.D(att_sel), .en(_2p), .Q(register_32_q), .clk(en), .clr(\new ));
  bcd bcd_3 (.attempt_2({_3_h_1t, _3_h_2t}), .attempt(register_33_q));
  Register register_33 (.D(att_sel), .en(_3p), .Q(register_33_q), .clk(en), .clr(\new ));
  bcd bcd_4 (.attempt_2({_4_h_1t, _4_h_2t}), .attempt(register_34_q));
  Register register_34 (.D(att_sel), .en(_4p), .Q(register_34_q), .clk(en), .clr(\new ));
  bcd bcd_5 (.attempt_2({_5_h_1t, _5_h_2t}), .attempt(register_35_q));
  Register register_35 (.D(att_sel), .en(_5p), .Q(register_35_q), .clk(en), .clr(\new ));
  Register register_36 (.D(_1f), .en(_6p), .Q({register_36_q, _6_h_1ch}), .clk(en), .clr(\new ));
  Register register_37 (.D(_1f), .en(_7p), .Q({register_37_q, _7_h_1ch}), .clk(en), .clr(\new ));
  Register register_38 (.D(_1f), .en(_8p), .Q({register_38_q, _8_h_1ch}), .clk(en), .clr(\new ));
  Register register_39 (.D(_1f), .en(_9p), .Q({register_39_q, _9_h_1ch}), .clk(en), .clr(\new ));
  Register register_40 (.D(_1f), .en(_10p), .Q({register_40_q, _10_h_1ch}), .clk(en), .clr(\new ));
  Register register_41 (.D(_2f), .en(_6p), .Q({register_41_q, _6_h_2ch}), .clk(en), .clr(\new ));
  Register register_42 (.D(_3f), .en(_6p), .Q({register_42_q, _6_h_3ch}), .clk(en), .clr(\new ));
  Register register_43 (.D(_3f), .en(_7p), .Q({register_43_q, _7_h_3ch}), .clk(en), .clr(\new ));
  Register register_44 (.D(_2f), .en(_7p), .Q({register_44_q, _7_h_2ch}), .clk(en), .clr(\new ));
  Register register_45 (.D(_2f), .en(_8p), .Q({register_45_q, _8_h_2ch}), .clk(en), .clr(\new ));
  Register register_46 (.D(_3f), .en(_8p), .Q({register_46_q, _8_h_3ch}), .clk(en), .clr(\new ));
  Register register_47 (.D(_3f), .en(_9p), .Q({register_47_q, _9_h_3ch}), .clk(en), .clr(\new ));
  Register register_48 (.D(_2f), .en(_9p), .Q({register_48_q, _9_h_2ch}), .clk(en), .clr(\new ));
  Register register_49 (.D(_3f), .en(_10p), .Q({register_49_q, _10_h_3ch}), .clk(en), .clr(\new ));
  Register register_50 (.D(_2f), .en(_10p), .Q({register_50_q, _10_h_2ch}), .clk(en), .clr(\new ));
  Register register_51 (.D(_4f), .en(_6p), .Q({register_51_q, _6_h_4ch}), .clk(en), .clr(\new ));
  Register register_52 (.D(_4f), .en(_7p), .Q({register_52_q, _7_h_4ch}), .clk(en), .clr(\new ));
  Register register_53 (.D(_4f), .en(_8p), .Q({register_53_q, _8_h_4ch}), .clk(en), .clr(\new ));
  Register register_54 (.D(_4f), .en(_9p), .Q({register_54_q, _9_h_4ch}), .clk(en), .clr(\new ));
  Register register_55 (.D(_4f), .en(_10p), .Q({register_55_q, _10_h_4ch}), .clk(en), .clr(\new ));
  Hex_Digit_Display hex_digit_display_9 (.value(_1_h_1ch));  // open: dp
  Hex_Digit_Display hex_digit_display_10 (.value(_2_h_1ch));  // open: dp
  Hex_Digit_Display hex_digit_display_11 (.value(_3_h_1ch));  // open: dp
  Hex_Digit_Display hex_digit_display_12 (.value(_4_h_1ch));  // open: dp
  Hex_Digit_Display hex_digit_display_13 (.value(_5_h_1ch));  // open: dp
  Register register_56 (.D({bullsout, buill_tek}), .en(_6p), .Q({register_56_q, _6_h_b}), .clk(en), .clr(\new ));
  Register register_57 (.D({bullsout, buill_tek}), .en(_7p), .Q({register_57_q, _7_h_b}), .clk(en), .clr(\new ));
  Hex_Digit_Display hex_digit_display_14 (.value(_1_h_2ch));  // open: dp
  Hex_Digit_Display hex_digit_display_15 (.value(_2_h_2ch));  // open: dp
  Hex_Digit_Display hex_digit_display_16 (.value(_3_h_2ch));  // open: dp
  Hex_Digit_Display hex_digit_display_17 (.value(_4_h_2ch));  // open: dp
  Hex_Digit_Display hex_digit_display_18 (.value(_5_h_2ch));  // open: dp
  Register register_58 (.D({cowsout, cow_tek}), .en(_6p), .Q({register_58_q, _6_h_c}), .clk(en), .clr(\new ));
  Register register_59 (.D({cowsout, cow_tek}), .en(_7p), .Q({register_59_q, _7_h_c}), .clk(en), .clr(\new ));
  Register register_60 (.D({bullsout, buill_tek}), .en(_8p), .Q({register_60_q, _8_h_b}), .clk(en), .clr(\new ));
  Register register_61 (.D({cowsout, cow_tek}), .en(_8p), .Q({register_61_q, _8_h_c}), .clk(en), .clr(\new ));
  Register register_62 (.D({cowsout, cow_tek}), .en(_9p), .Q({register_62_q, _9_h_c}), .clk(en), .clr(\new ));
  Register register_63 (.D({bullsout, buill_tek}), .en(_9p), .Q({register_63_q, _9_h_b}), .clk(en), .clr(\new ));
  Register register_64 (.D({cowsout, cow_tek}), .en(_10p), .Q({register_64_q, _10_h_c}), .clk(en), .clr(\new ));
  Register register_65 (.D({bullsout, buill_tek}), .en(_10p), .Q({register_65_q, _10_h_b}), .clk(en), .clr(\new ));
  Hex_Digit_Display hex_digit_display_19 (.value(_1_h_4ch));  // open: dp
  Hex_Digit_Display hex_digit_display_20 (.value(_1_h_3ch));  // open: dp
  Hex_Digit_Display hex_digit_display_21 (.value(_2_h_3ch));  // open: dp
  Hex_Digit_Display hex_digit_display_22 (.value(_2_h_4ch));  // open: dp
  Hex_Digit_Display hex_digit_display_23 (.value(_3_h_3ch));  // open: dp
  Hex_Digit_Display hex_digit_display_24 (.value(_3_h_4ch));  // open: dp
  Hex_Digit_Display hex_digit_display_25 (.value(_4_h_3ch));  // open: dp
  Hex_Digit_Display hex_digit_display_26 (.value(_4_h_4ch));  // open: dp
  Hex_Digit_Display hex_digit_display_27 (.value(_5_h_3ch));  // open: dp
  Hex_Digit_Display hex_digit_display_28 (.value(_5_h_4ch));  // open: dp
  bcd bcd_6 (.attempt_2({_6_h_1t, _6_h_2t}), .attempt(register_66_q));
  Register register_66 (.D(att_sel), .en(_6p), .Q(register_66_q), .clk(en), .clr(\new ));
  bcd bcd_7 (.attempt_2({_7_h_1t, _7_h_2t}), .attempt(register_67_q));
  Register register_67 (.D(att_sel), .en(_7p), .Q(register_67_q), .clk(en), .clr(\new ));
  Register register_68 (.D(att_sel), .en(_8p), .Q(register_68_q), .clk(en), .clr(\new ));
  Register register_69 (.D(att_sel), .en(_9p), .Q(register_69_q), .clk(en), .clr(\new ));
  Register register_70 (.D(att_sel), .en(_10p), .Q(register_70_q), .clk(en), .clr(\new ));
  Hex_Digit_Display hex_digit_display_29 (.value(_1_h_b));  // open: dp
  Hex_Digit_Display hex_digit_display_30 (.value(_2_h_b));  // open: dp
  Hex_Digit_Display hex_digit_display_31 (.value(_3_h_b));  // open: dp
  Hex_Digit_Display hex_digit_display_32 (.value(_4_h_b));  // open: dp
  Hex_Digit_Display hex_digit_display_33 (.value(_5_h_b));  // open: dp
  bcd bcd_8 (.attempt_2({_8_h_1t, _8_h_2t}), .attempt(register_68_q));
  bcd bcd_9 (.attempt_2({_9_h_1t, _9_h_2t}), .attempt(register_69_q));
  bcd bcd_10 (.attempt_2({_10_h_1t, _10_h_2t}), .attempt(register_70_q));
  Hex_Digit_Display hex_digit_display_34 (.value(_1_h_c));  // open: dp
  Hex_Digit_Display hex_digit_display_35 (.value(_2_h_c));  // open: dp
  Hex_Digit_Display hex_digit_display_36 (.value(_3_h_c));  // open: dp
  Hex_Digit_Display hex_digit_display_37 (.value(_4_h_c));  // open: dp
  Hex_Digit_Display hex_digit_display_38 (.value(_5_h_c));  // open: dp
  Comparator comparator_1 (.a(addr), .b(8'hf4), .eq(comparator_1_eq));  // open: gt, lt
  Hex_Digit_Display hex_digit_display_39 (.value(_1_h_1t));  // open: dp
  Hex_Digit_Display hex_digit_display_40 (.value(_2_h_1t));  // open: dp
  Hex_Digit_Display hex_digit_display_41 (.value(_3_h_1t));  // open: dp
  Hex_Digit_Display hex_digit_display_42 (.value(_4_h_1t));  // open: dp
  Hex_Digit_Display hex_digit_display_43 (.value(_5_h_1t));  // open: dp
  and and_1 (en, comparator_1_eq, rd_rw);
  Hex_Digit_Display hex_digit_display_44 (.value(_1_h_2t));  // open: dp
  Hex_Digit_Display hex_digit_display_45 (.value(_2_h_2t));  // open: dp
  Hex_Digit_Display hex_digit_display_46 (.value(_3_h_2t));  // open: dp
  Hex_Digit_Display hex_digit_display_47 (.value(_4_h_2t));  // open: dp
  Hex_Digit_Display hex_digit_display_48 (.value(_5_h_2t));  // open: dp
  Counter #(.width(4), .max('h9)) counter_1 (.Q(counter_1_q), .clk(en), .clr(\new ));  // open: load, D, count, carry
  Decoder #(.select(4), .enable("false")) decoder_1 (
    .out0(_1p), .out1(_2p), .out2(_3p), .out3(_4p), .out4(_5p), .out5(_6p), .out6(_7p), .out7(_8p),
    .out8(_9p), .out9(_10p), .sel(counter_1_q));  // open: out10, out11, out12, out13, out14, out15
  Multiplexer #(.select(2), .width(8)) multiplexer_1 (
    .in0({8{1'b0}}), .in1({8{1'b0}}), .in3({8{1'b0}}), .out(_1d), .sel(sel));  // open: in2, en
  Multiplexer #(.select(2), .width(8)) multiplexer_2 (
    .in0({8{1'b0}}), .in1(8'h7e), .in3({8{1'b0}}), .out(_2d), .sel(sel));  // open: in2, en
  Multiplexer #(.select(2), .width(8)) multiplexer_3 (
    .in0({8{1'b0}}), .in1(8'h2), .in3({8{1'b0}}), .out(_3d), .sel(sel));  // open: in2, en
  Multiplexer #(.select(2), .width(8)) multiplexer_4 (
    .in0({8{1'b0}}), .in1(8'h2), .in3({8{1'b0}}), .out(_4d), .sel(sel));  // open: in2, en
  Multiplexer #(.select(2), .width(8)) multiplexer_5 (
    .in0({8{1'b0}}), .in1(8'h2), .in3({8{1'b0}}), .out(_5d), .sel(sel));  // open: in2, en
  Multiplexer #(.select(2), .width(8)) multiplexer_6 (
    .in0({8{1'b0}}), .in1(8'h6), .in3({8{1'b0}}), .out(_6d), .sel(sel));  // open: in2, en
  Multiplexer #(.select(2), .width(8)) multiplexer_7 (
    .in0({8{1'b0}}), .in1({8{1'b0}}), .in3(8'h60), .out(_7d), .sel(sel));  // open: in2, en
  Multiplexer #(.select(2), .width(8)) multiplexer_8 (
    .in0({8{1'b0}}), .in1(8'h3c), .in3(8'h18), .out(_8d), .sel(sel));  // open: in2, en
  Hex_Digit_Display hex_digit_display_49 (.value(_6_h_1ch));  // open: dp
  Hex_Digit_Display hex_digit_display_50 (.value(_7_h_1ch));  // open: dp
  Hex_Digit_Display hex_digit_display_51 (.value(_8_h_1ch));  // open: dp
  Hex_Digit_Display hex_digit_display_52 (.value(_9_h_1ch));  // open: dp
  Hex_Digit_Display hex_digit_display_53 (.value(_10_h_1ch));  // open: dp
  Hex_Digit_Display hex_digit_display_54 (.value(_6_h_2ch));  // open: dp
  Hex_Digit_Display hex_digit_display_55 (.value(_7_h_2ch));  // open: dp
  Hex_Digit_Display hex_digit_display_56 (.value(_8_h_2ch));  // open: dp
  Hex_Digit_Display hex_digit_display_57 (.value(_9_h_2ch));  // open: dp
  Hex_Digit_Display hex_digit_display_58 (.value(_10_h_2ch));  // open: dp
  Multiplexer #(.select(2), .width(8)) multiplexer_9 (
    .in0({8{1'b0}}), .in1(8'h42), .in3(8'h6), .out(_9d), .sel(sel));  // open: in2, en
  Multiplexer #(.select(2), .width(8)) multiplexer_10 (
    .in0({8{1'b0}}), .in1(8'h42), .in3(8'h18), .out(_10d), .sel(sel));  // open: in2, en
  Multiplexer #(.select(2), .width(8)) multiplexer_11 (
    .in0({8{1'b0}}), .in1(8'h3c), .in3(8'h6), .out(_11d), .sel(sel));  // open: in2, en
  Multiplexer #(.select(2), .width(8)) multiplexer_12 (
    .in0({8{1'b0}}), .in1({8{1'b0}}), .in3(8'h18), .out(_12d), .sel(sel));  // open: in2, en
  Multiplexer #(.select(2), .width(8)) multiplexer_13 (
    .in0({8{1'b0}}), .in1(8'h24), .in3(8'h60), .out(_13d), .sel(sel));  // open: in2, en
  Multiplexer #(.select(2), .width(8)) multiplexer_14 (
    .in0({8{1'b0}}), .in1(8'h52), .in3({8{1'b0}}), .out(_14d), .sel(sel));  // open: in2, en
  Multiplexer #(.select(2), .width(8)) multiplexer_15 (
    .in0({8{1'b0}}), .in1(8'h52), .in3(8'h6e), .out(_15d), .sel(sel));  // open: in2, en
  Multiplexer #(.select(2), .width(8)) multiplexer_16 (
    .in0({8{1'b0}}), .in1(8'h4a), .in3({8{1'b0}}), .out(_16d), .sel(sel));  // open: in2, en
  Hex_Digit_Display hex_digit_display_59 (.value(_6_h_3ch));  // open: dp
  Hex_Digit_Display hex_digit_display_60 (.value(_6_h_4ch));  // open: dp
  Hex_Digit_Display hex_digit_display_61 (.value(_7_h_4ch));  // open: dp
  Hex_Digit_Display hex_digit_display_62 (.value(_7_h_3ch));  // open: dp
  Hex_Digit_Display hex_digit_display_63 (.value(_8_h_3ch));  // open: dp
  Hex_Digit_Display hex_digit_display_64 (.value(_8_h_4ch));  // open: dp
  Hex_Digit_Display hex_digit_display_65 (.value(_9_h_4ch));  // open: dp
  Hex_Digit_Display hex_digit_display_66 (.value(_9_h_3ch));  // open: dp
  Hex_Digit_Display hex_digit_display_67 (.value(_10_h_4ch));  // open: dp
  Hex_Digit_Display hex_digit_display_68 (.value(_10_h_3ch));  // open: dp
  Hex_Digit_Display hex_digit_display_69 (.value(_6_h_b));  // open: dp
  Hex_Digit_Display hex_digit_display_70 (.value(_7_h_b));  // open: dp
  Hex_Digit_Display hex_digit_display_71 (.value(_8_h_b));  // open: dp
  Hex_Digit_Display hex_digit_display_72 (.value(_9_h_b));  // open: dp
  Hex_Digit_Display hex_digit_display_73 (.value(_10_h_b));  // open: dp
  Multiplexer #(.select(2), .width(8)) multiplexer_17 (
    .in0({8{1'b0}}), .in1(8'h24), .in3(8'h3e), .out(_17d), .sel(sel));  // open: in2, en
  Multiplexer #(.select(2), .width(8)) multiplexer_18 (
    .in0({8{1'b0}}), .in1({8{1'b0}}), .in3(8'h10), .out(_18d), .sel(sel));  // open: in2, en
  Multiplexer #(.select(2), .width(8)) multiplexer_19 (
    .in0({8{1'b0}}), .in1(8'h3c), .in3(8'h20), .out(_19d), .sel(sel));  // open: in2, en
  Multiplexer #(.select(2), .width(8)) multiplexer_20 (
    .in0({8{1'b0}}), .in1(8'h4a), .in3(8'h20), .out(_20d), .sel(sel));  // open: in2, en
  Multiplexer #(.select(2), .width(8)) multiplexer_21 (
    .in0({8{1'b0}}), .in1(8'h4a), .in3(8'h1e), .out(_21d), .sel(sel));  // open: in2, en
  Multiplexer #(.select(2), .width(8)) multiplexer_22 (
    .in0({8{1'b0}}), .in1(8'h4a), .in3({8{1'b0}}), .out(_22d), .sel(sel));  // open: in2, en
  Multiplexer #(.select(2), .width(8)) multiplexer_23 (
    .in0({8{1'b0}}), .in1(8'h7a), .in3(8'h62), .out(_23d), .sel(sel));  // open: in2, en
  Multiplexer #(.select(2), .width(8)) multiplexer_24 (
    .in0({8{1'b0}}), .in1({8{1'b0}}), .in3({8{1'b0}}), .out(_24d), .sel(sel));  // open: in2, en
  Hex_Digit_Display hex_digit_display_74 (.value(_6_h_c));  // open: dp
  Hex_Digit_Display hex_digit_display_75 (.value(_7_h_c));  // open: dp
  Hex_Digit_Display hex_digit_display_76 (.value(_8_h_c));  // open: dp
  Hex_Digit_Display hex_digit_display_77 (.value(_9_h_c));  // open: dp
  Hex_Digit_Display hex_digit_display_78 (.value(_10_h_c));  // open: dp
  Multiplexer #(.select(2), .width(8)) multiplexer_25 (
    .in0({8{1'b0}}), .in1(8'h7e), .in3({8{1'b0}}), .out(_25d), .sel(sel));  // open: in2, en
  Multiplexer #(.select(2), .width(8)) multiplexer_26 (
    .in0({8{1'b0}}), .in1(8'h20), .in3({8{1'b0}}), .out(_26d), .sel(sel));  // open: in2, en
  Multiplexer #(.select(2), .width(8)) multiplexer_27 (
    .in0({8{1'b0}}), .in1(8'h40), .in3({8{1'b0}}), .out(_27d), .sel(sel));  // open: in2, en
  Multiplexer #(.select(2), .width(8)) multiplexer_28 (
    .in0({8{1'b0}}), .in1(8'h40), .in3({8{1'b0}}), .out(_28d), .sel(sel));  // open: in2, en
  Multiplexer #(.select(2), .width(8)) multiplexer_29 (
    .in0({8{1'b0}}), .in1(8'h20), .in3({8{1'b0}}), .out(_29d), .sel(sel));  // open: in2, en
  Multiplexer #(.select(2), .width(8)) multiplexer_30 (
    .in0({8{1'b0}}), .in1({8{1'b0}}), .in3({8{1'b0}}), .out(_30d), .sel(sel));  // open: in2, en
  Multiplexer #(.select(2), .width(8)) multiplexer_31 (
    .in0({8{1'b0}}), .in1({8{1'b0}}), .in3({8{1'b0}}), .out(_31d), .sel(sel));  // open: in2, en
  Multiplexer #(.select(2), .width(8)) multiplexer_32 (
    .in0({8{1'b0}}), .in1({8{1'b0}}), .in3({8{1'b0}}), .out(_32d), .sel(sel));  // open: in2, en
  Hex_Digit_Display hex_digit_display_79 (.value(_6_h_1t));  // open: dp
  Hex_Digit_Display hex_digit_display_80 (.value(_7_h_1t));  // open: dp
  Hex_Digit_Display hex_digit_display_81 (.value(_8_h_1t));  // open: dp
  Hex_Digit_Display hex_digit_display_82 (.value(_9_h_1t));  // open: dp
  Hex_Digit_Display hex_digit_display_83 (.value(_10_h_1t));  // open: dp
  INPUT_IO input_io_1 (
    ._1(_1), ._2(_2), ._3(_3), ._4(_4), ._5(_5), ._6(_6), ._7(_7), ._8(_8), ._9(_9), ._0(_0), .ok(ok),
    .addr(addr), .data_in(input_io_1_data_in), .ok_2(input_io_1_ok_2), .new_vod(nv), .\new (\new ),
    .clk(cpu_core_1_clk), ._1f(_1f), ._2f(_2f), ._3f(_3f), ._4f(_4f), .data_gen_code(input_io_1_data_gen_code));
  // Probe on addr
  Hex_Digit_Display hex_digit_display_84 (.value(_6_h_2t));  // open: dp
  Hex_Digit_Display hex_digit_display_85 (.value(_7_h_2t));  // open: dp
  Hex_Digit_Display hex_digit_display_86 (.value(_8_h_2t));  // open: dp
  Hex_Digit_Display hex_digit_display_87 (.value(_9_h_2t));  // open: dp
  Hex_Digit_Display hex_digit_display_88 (.value(_10_h_2t));  // open: dp
  CPU_CORE cpu_core_1 (
    .ok(input_io_1_ok_2), .data_out(cpu_core_1_data_out), .clk(cpu_core_1_clk), .addr_out(addr),
    .addr_in(cpu_core_1_addr_in), .data_gen_code(input_io_1_data_gen_code), .\new (\new ),
    .data_in(input_io_1_data_in), .rd_rw(rd_rw), .over(blk));
  Comparator comparator_2 (.a(8'h19), .b(att_sel), .eq(blk));  // open: gt, lt
  Comparator #(.width(1)) comparator_3 (.a(win), .b(1'b1), .eq(comparator_3_eq));  // open: gt, lt
  Multiplexer #(.width(2), .enable("false")) multiplexer_33 (
    .in0(2'b00), .in1(2'b01), .out(multiplexer_33_out), .sel(blk));
  Multiplexer #(.width(2), .enable("false")) multiplexer_34 (
    .in0(2'b00), .in1(2'b11), .out(multiplexer_34_out), .sel(comparator_3_eq));
  // Probe on att_sel
  assign sel = multiplexer_33_out | multiplexer_34_out;  // OR_Gate or_1, 2 bits wide
  // Probe on cpu_core_1_addr_in
  bcd bcd_11 (.attempt_2({_1tries_tek, _2tries_tek}), .attempt(att_sel));
  OUTPUT_IO output_io_1 (
    .data_out(cpu_core_1_data_out), .bull({bullsout, buill_tek}), .cow({cowsout, cow_tek}),
    .attempt(att_sel), .win(win), .addr(cpu_core_1_addr_in), .in_1(\new ), ._2(nv));
  block block_1 (.signal(_1), .nv(nv), .nw(\new ), .knp(_1s));
  block block_2 (.signal(_2), .nv(nv), .nw(\new ), .knp(_2s));
  block block_3 (.signal(_3), .nv(nv), .nw(\new ), .knp(_3s));
  block block_4 (.signal(_4), .nv(nv), .nw(\new ), .knp(_4s));
  block block_5 (.signal(_5), .nv(nv), .nw(\new ), .knp(_5s));
  block block_6 (.signal(_6), .nv(nv), .nw(\new ), .knp(_6s));
  block block_7 (.signal(_7), .nv(nv), .nw(\new ), .knp(_7s));
  block block_8 (.signal(_8), .nv(nv), .nw(\new ), .knp(_8s));
  block block_9 (.signal(_9), .nv(nv), .nw(\new ), .knp(_9s));
  block block_10 (.signal(_0), .nv(nv), .nw(\new ), .knp(_0s));

  // Other names for the same wires on the sheet: _1tek[3:0] = _1f[3:0]; _2tek[3:0] = _2f[3:0]; _3tek[3:0] = _3f[3:0];
  //   _4tek[3:0] = _4f[3:0]; attout[7:0] = att_sel; bullsout[3:0] = buill_tek; cowsout[3:0] = cow_tek; nvs = nv;
  //   oks = ok; win_sel = win

  // Notes on the sheet:
  //   КОД
  //   Быки и Коровы
  //   Быки
  //   Коровы
  //   игру
  //   Попытка
  //   Начать новую 
  //   КОД
  //   Быки
  //   Коровы
  //   Попытка
  //   КОД
  //   Быки
  //   Коровы
  //   Попытка
endmodule

module CPU_CORE (
  input  \new ,
  input  over,
  input  ok,
  input  [7:0] data_in,
  input  [7:0] data_gen_code,
  output [7:0] addr_in,
  output [7:0] addr_out,
  output rd_rw,
  output clk,
  output [7:0] data_out
);

  wire and_1_out, and_2_out, and_3_out, and_4_out, and_5_out, and_6_out, comparator_4_eq, comparator_5_eq,
       comparator_6_eq, comparator_7_eq, comparator_9_eq, comparator_10_eq, comparator_12_eq, dat_ins, mem,
       or_1_out, or_3_out, or_4_out, ozu, pull_resistor_1_node, pull_resistor_2_node, pull_resistor_3_node,
       pull_resistor_8_node, pull_resistor_13_node, pzu, sel_out;
  wire [7:0] addr_f, cdm_8_1_data_out, cdm_8_1_pc, cdm_8_1_ps, cdm_8_1_r0, cdm_8_1_r1, cdm_8_1_r2,
       cdm_8_1_r3, cdm_8_1_sp, data, data_in_t, data_OUT_t, data_out_t_t, dt_out_cd;

  Clock clock_1 (.out(clk));
  // Probe on addr_in
  // Probe on addr_in
  // Probe on cdm_8_1_r1
  // Probe on cdm_8_1_r0
  and and_1 (and_1_out, and_2_out, ~over);  // AND_Gate
  and and_2 (and_2_out, clk, ~ok);  // AND_Gate
  Pull_Resistor pull_resistor_1 (.node(pull_resistor_1_node));
  Comparator comparator_1 (.a(addr_in), .b(8'hf0), .eq(pull_resistor_1_node));  // open: gt, lt
  Pull_Resistor pull_resistor_2 (.node(pull_resistor_2_node));
  Comparator comparator_2 (.a(addr_in), .b(8'hf1), .eq(pull_resistor_2_node));  // open: gt, lt
  Pull_Resistor pull_resistor_3 (.node(pull_resistor_3_node));
  Comparator comparator_3 (.a(addr_in), .b(8'hf2), .eq(pull_resistor_3_node));  // open: gt, lt
  Comparator comparator_4 (.a(addr_in), .b(8'hf3), .eq(comparator_4_eq));  // open: gt, lt
  Pull_Resistor pull_resistor_4 (.node(comparator_4_eq));
  Comparator comparator_5 (.a(addr_in), .b(8'he5), .eq(comparator_5_eq));  // open: gt, lt
  Pull_Resistor pull_resistor_5 (.node(comparator_5_eq));
  Comparator comparator_6 (.a(addr_in), .b(8'he6), .eq(comparator_6_eq));  // open: gt, lt
  Pull_Resistor pull_resistor_6 (.node(comparator_6_eq));
  Comparator comparator_7 (.a(addr_in), .b(8'he7), .eq(comparator_7_eq));  // open: gt, lt
  Pull_Resistor pull_resistor_7 (.node(comparator_7_eq));
  Pull_Resistor pull_resistor_8 (.node(pull_resistor_8_node));
  Comparator comparator_8 (.a(addr_in), .b(8'he8), .eq(pull_resistor_8_node));  // open: gt, lt
  // Probe on cdm_8_1_r2
  // Probe on cdm_8_1_pc
  // Probe on cdm_8_1_r3
  or or_1 (or_1_out, pull_resistor_1_node, pull_resistor_2_node, pull_resistor_3_node, comparator_4_eq);
  or or_2 (sel_out, comparator_5_eq, comparator_6_eq, comparator_7_eq, pull_resistor_8_node);
  // Probe on cdm_8_1_ps
  // Probe on cdm_8_1_sp
  and and_3 (and_3_out, rd_rw, ~ok);  // AND_Gate
  CdM_8 cdm_8_1 (
    .data_code_prime(dat_ins), .R0(cdm_8_1_r0), .R1(cdm_8_1_r1), .mem(mem), .R2(cdm_8_1_r2),
    .load_st_prime(rd_rw), .R3(cdm_8_1_r3), .addr(addr_in), .PC(cdm_8_1_pc), .SP(cdm_8_1_sp),
    .data_out(cdm_8_1_data_out), .data_in(data_OUT_t), .PS(cdm_8_1_ps), .clk(and_1_out), .rset(\new ));  // open: page, IAck, IRQ, vector, shadow
  assign data_in_t = and_3_out ? data : 8'bz;  // Controlled_Buffer controlled_buffer_1
  assign data = and_4_out ? cdm_8_1_data_out : 8'bz;  // Controlled_Buffer controlled_buffer_2
  Multiplexer #(.width(8), .enable("false")) multiplexer_1 (
    .in0(data_in_t), .in1(data_in), .out(data_out_t_t), .sel(or_1_out));
  // Probe on data_out_t_t
  Multiplexer #(.width(8), .enable("false")) multiplexer_2 (
    .in0(data_in_t), .in1(data_gen_code), .out(dt_out_cd), .sel(sel_out));
  // Probe on dt_out_cd
  and and_4 (and_4_out, ~rd_rw, ~ok);  // AND_Gate
  Decoder decoder_1 (.out0(pzu), .out1(ozu), .sel(dat_ins), .en(and_5_out));
  and and_5 (and_5_out, mem, ~ok);  // AND_Gate
  Pull_Resistor pull_resistor_9 (.node(pzu));
  Pull_Resistor pull_resistor_10 (.node(ozu));
  Comparator comparator_9 (.a(addr_in), .b(8'hf5), .eq(comparator_9_eq));  // open: gt, lt
  Pull_Resistor pull_resistor_11 (.node(comparator_9_eq));
  Comparator comparator_10 (.a(addr_in), .b(8'hf6), .eq(comparator_10_eq));  // open: gt, lt
  Pull_Resistor pull_resistor_12 (.node(comparator_10_eq));
  Pull_Resistor pull_resistor_13 (.node(pull_resistor_13_node));
  Comparator comparator_11 (.a(addr_in), .b(8'hf7), .eq(pull_resistor_13_node));  // open: gt, lt
  Comparator comparator_12 (.a(addr_in), .b(8'hf8), .eq(comparator_12_eq));  // open: gt, lt
  Pull_Resistor pull_resistor_14 (.node(comparator_12_eq));
  or or_3 (or_3_out, ozu, ok);
  Multiplexer #(.width(8), .enable("false")) multiplexer_3 (.in0(addr_in), .in1(8'hf4), .out(addr_f), .sel(ok));
  ROM rom_1 (.addr(addr_f), .data(data), .sel(pzu));
  RAM ram_1 (.addr(addr_f), .data(data), .sel(or_3_out), .clk(clk), .ld(and_6_out));  // open: clr
  and and_6 (and_6_out, rd_rw, ~ok);  // AND_Gate
  or or_4 (or_4_out, comparator_9_eq, comparator_10_eq, pull_resistor_13_node, comparator_12_eq);
  assign data = ok ? 8'h1 : 8'bz;  // Controlled_Buffer controlled_buffer_3
  assign data_out = or_4_out ? data : 8'bz;  // Controlled_Buffer controlled_buffer_4
  Multiplexer #(.width(8), .enable("false")) multiplexer_4 (
    .in0(data_out_t_t), .in1(dt_out_cd), .out(data_OUT_t), .sel(sel_out));

  assign addr_out = addr_in;

  // Other names for the same wires on the sheet: addr[7:0] = addr_in

  // Notes on the sheet:
  //   contents of rom_1 (hex, n*v repeats v):
  //   d0 f5 d1 0 a1 d0 f6 a1 d0 f7 a1 d0 f8 a1 d0 f8 b1 5 e0 16 ee d2 d0 f4 b1 d3 1 77 e1 20 ee 22 ee 16
  //   d0 f5 d1 0 a1 d0 f6 a1 d2 0 d0 f0 b1 d0 e5 b3 77 e1 36 8e d0 f1 b1 d0 e6 b3 77 e1 40 8e d0 f2 b1 d0
  //   e7 b3 77 e1 4a 8e d0 f3 b1 d0 e8 b3 77 e1 54 8e d0 f5 a2 d3 4 7b e1 61 d0 f8 d1 1 a1 d2 0 d0 f0 b1
  //   d0 e6 b3 77 e1 6d 8e d0 e7 b3 77 e1 74 8e d0 e8 b3 77 e1 7b 8e d0 f1 b1 d0 e5 b3 77 e1 85 8e d0 e7
  //   b3 77 e1 8c 8e d0 e8 b3 77 e1 93 8e d0 f2 b1 d0 e5 b3 77 e1 9d 8e d0 e6 b3 77 e1 a4 8e d0 e8 b3 77
  //   e1 ab 8e d0 f3 b1 d0 e5 b3 77 e1 b5 8e d0 e6 b3 77 e1 bc 8e d0 e7 b3 77 e1 c3 8e d0 f6 a2 d0 f7 b1
  //   8d a1 d0 f4 d1 0 a1 ee e d4
endmodule

module INPUT_IO (
  input  _1,
  input  _2,
  input  _3,
  input  _4,
  input  _5,
  input  _6,
  input  new_vod,
  input  \new ,
  input  _7,
  input  _8,
  input  _9,
  input  [7:0] addr,
  input  _0,
  input  ok,
  input  clk,
  output [7:0] data_in,
  output [7:0] _1f,
  output [7:0] _2f,
  output ok_2,
  output [7:0] _3f,
  output [7:0] _4f,
  output [7:0] data_gen_code
);

  wire comparator_1_eq, decoder_1_out0, decoder_1_out1, decoder_1_out2, decoder_1_out3, decoder_1_out4,
       or_1_out, priority_encoder_1_gs;
  wire [2:0] counter_1_q;
  wire [3:0] priority_encoder_1_out;
  wire [7:0] _1sec, _2sec, _3sec, _4sec, and_1_out, bit_extender_1_out, ok_f;

  Hex_Digit_Display hex_digit_display_1 (.value(_1f[3:0]));  // open: dp
  Register register_1 (.D(bit_extender_1_out), .en(1'b1), .Q(_1f), .clk(decoder_1_out1), .clr(decoder_1_out0));
  Hex_Digit_Display hex_digit_display_2 (.value(_2f[3:0]));  // open: dp
  Register register_2 (.D(bit_extender_1_out), .en(1'b1), .Q(_2f), .clk(decoder_1_out2), .clr(decoder_1_out0));
  Hex_Digit_Display hex_digit_display_3 (.value(_3f[3:0]));  // open: dp
  Register register_3 (.D(bit_extender_1_out), .en(1'b1), .Q(_3f), .clk(decoder_1_out3), .clr(decoder_1_out0));
  Priority_Encoder #(.select(4)) priority_encoder_1 (
    .in0(_0), .in1(_1), .in2(_2), .in3(_3), .in4(_4), .in5(_5), .in6(_6), .in7(_7), .in8(_8), .in9(_9),
    .out(priority_encoder_1_out), .gs(priority_encoder_1_gs), .en_in(1'b1));  // open: in10, in11, in12, in13, in14, in15, en_out
  Hex_Digit_Display hex_digit_display_4 (.value(_4f[3:0]));  // open: dp
  Register register_4 (.D(bit_extender_1_out), .en(1'b1), .Q(_4f), .clk(decoder_1_out4), .clr(decoder_1_out0));
  assign bit_extender_1_out = {{4{1'b0}}, priority_encoder_1_out};  // Bit_Extender bit_extender_1
  Counter #(.width(3), .max('h7)) counter_1 (
    .Q(counter_1_q), .clk(priority_encoder_1_gs), .clr(or_1_out));  // open: load, D, count, carry
  or or_1 (or_1_out, new_vod, \new );
  assign ok_f = {{7{1'b0}}, ok};  // Bit_Extender bit_extender_2
  Decoder #(.select(3), .enable("false")) decoder_1 (
    .out0(decoder_1_out0), .out1(decoder_1_out1), .out2(decoder_1_out2), .out3(decoder_1_out3),
    .out4(decoder_1_out4), .sel(counter_1_q));  // open: out5, out6, out7
  GEN_CODE gen_code_1 (.clk(clk), .\new (\new ), ._1sec(_1sec), ._2sec(_2sec), ._3sec(_3sec), ._4sec(_4sec));
  Multiplexer #(.select(3), .width(8)) multiplexer_1 (
    .in0(_1f), .in1(_2f), .in2(_3f), .in3(_4f), .out(data_in), .sel(addr[2:0]), .en(comparator_1_eq));  // open: in4, in5, in6, in7
  assign and_1_out = addr & 8'hf0;  // AND_Gate and_1, 8 bits wide
  Comparator comparator_1 (.a(and_1_out), .b(8'hf0), .eq(comparator_1_eq));  // open: gt, lt
  Multiplexer #(.select(4), .width(8), .enable("false")) multiplexer_2 (
    .in5(_1sec), .in6(_2sec), .in7(_3sec), .in8(_4sec), .out(data_gen_code), .sel(addr[3:0]));  // open: in0, in1, in2, in3, in4, in9, in10, in11, in12, in13, in14, in15

  assign ok_2 = ok;
endmodule

module OUTPUT_IO (
  input  in_1,
  input  _2,
  input  [7:0] data_out,
  input  [7:0] addr,
  output win,
  output [7:0] attempt,
  output [7:0] cow,
  output [7:0] bull
);

  wire comparator_1_eq, comparator_2_eq, comparator_3_eq, comparator_4_eq, en_attempt, en_bull, en_cow,
       en_win, logic_flag, or_1_out;
  wire [7:0] register_1_q;

  Hex_Digit_Display hex_digit_display_1 (.value(bull[7:4]));  // open: dp
  Hex_Digit_Display hex_digit_display_2 (.value(bull[3:0]));  // open: dp
  Hex_Digit_Display hex_digit_display_3 (.value(cow[7:4]));  // open: dp
  Hex_Digit_Display hex_digit_display_4 (.value(cow[3:0]));  // open: dp
  Comparator comparator_1 (.a(addr), .b(8'hf5), .eq(comparator_1_eq));  // open: gt, lt
  Comparator comparator_2 (.a(addr), .b(8'hf6), .eq(comparator_2_eq));  // open: gt, lt
  Comparator comparator_3 (.a(addr), .b(8'hf7), .eq(comparator_3_eq));  // open: gt, lt
  Comparator comparator_4 (.a(addr), .b(8'hf8), .eq(comparator_4_eq));  // open: gt, lt
  Hex_Digit_Display hex_digit_display_5 (.value(attempt[3:0]));  // open: dp
  Hex_Digit_Display hex_digit_display_6 (.value(attempt[7:4]));  // open: dp
  Pull_Resistor pull_resistor_1 (.node(comparator_1_eq));
  Pull_Resistor pull_resistor_2 (.node(comparator_2_eq));
  Pull_Resistor pull_resistor_3 (.node(comparator_3_eq));
  Pull_Resistor pull_resistor_4 (.node(comparator_4_eq));
  Register register_1 (.D(data_out), .en(1'b1), .Q(register_1_q), .clk(en_win), .clr(in_1));
  Register register_2 (.D(data_out), .en(1'b1), .Q(attempt), .clk(en_attempt), .clr(or_1_out));
  Register register_3 (.D(data_out), .en(1'b1), .Q(cow), .clk(en_cow), .clr(or_1_out));
  Register register_4 (.D(data_out), .en(1'b1), .Q(bull), .clk(en_bull), .clr(or_1_out));
  and and_1 (en_bull, comparator_1_eq, logic_flag);
  and and_2 (en_cow, comparator_2_eq, logic_flag);
  and and_3 (en_attempt, comparator_3_eq, logic_flag);
  and and_4 (en_win, comparator_4_eq, logic_flag);
  Hex_Digit_Display hex_digit_display_7 (.value(register_1_q[7:4]));  // open: dp
  Hex_Digit_Display hex_digit_display_8 (.value(register_1_q[3:0]));  // open: dp
  Bit_Extender #(.out_width(1)) bit_extender_1 (.in(register_1_q), .out(win));
  or or_1 (or_1_out, in_1, _2);
  Comparator comparator_5 (.a(data_out), .b({8{1'b0}}), .gt(logic_flag));  // open: eq, lt
  Pull_Resistor pull_resistor_5 (.node(logic_flag));

  // Other names for the same wires on the sheet: attempts[7:0] = attempt; bulls[7:0] = bull; cows[7:0] = cow
endmodule

module GEN_CODE (
  input  \new ,
  input  clk,
  output [7:0] _1sec,
  output [7:0] _2sec,
  output [7:0] _3sec,
  output [7:0] _4sec
);

  wire and_1_out, comparator_1_eq, comparator_2_eq, comparator_3_eq, comparator_4_eq, comparator_5_eq,
       comparator_6_eq, comparator_7_eq, comparator_8_eq, comparator_9_eq, comparator_10_eq,
       comparator_11_eq, comparator_12_eq, or_1_out, or_2_out;
  wire [7:0] and_2_out, and_3_out, and_4_out, and_5_out, random_1_out, random_2_out, random_3_out,
       random_4_out;

  or or_1 (or_1_out, and_1_out, \new );
  and and_1 (and_1_out, clk, or_2_out);
  Random random_1 (.clk(or_1_out), .out(random_1_out));  // open: next, clr
  Pull_Resistor pull_resistor_1 (.node(or_1_out));
  Random #(.seed(3)) random_2 (.clk(or_1_out), .out(random_2_out));  // open: next, clr
  Random #(.seed(7)) random_3 (.clk(or_1_out), .out(random_3_out));  // open: next, clr
  Random #(.seed(8)) random_4 (.clk(or_1_out), .out(random_4_out));  // open: next, clr
  assign and_2_out = random_1_out & 8'h7f;  // AND_Gate and_2, 8 bits wide
  assign and_3_out = random_2_out & 8'h7f;  // AND_Gate and_3, 8 bits wide
  assign and_4_out = random_3_out & 8'h7f;  // AND_Gate and_4, 8 bits wide
  assign and_5_out = random_4_out & 8'h7f;  // AND_Gate and_5, 8 bits wide
  Divider divider_1 (.a(and_2_out), .b(8'ha), .rem(_1sec));  // open: out, upper
  Divider divider_2 (.a(and_3_out), .b(8'ha), .rem(_2sec));  // open: out, upper
  Divider divider_3 (.a(and_4_out), .b(8'ha), .rem(_3sec));  // open: out, upper
  // Probe on _3sec
  Divider divider_4 (.a(and_5_out), .b(8'ha), .rem(_4sec));  // open: out, upper
  // Probe on _4sec
  // Probe on _1sec
  // Probe on _2sec
  Comparator comparator_1 (.a(_1sec), .b(_2sec), .eq(comparator_1_eq));  // open: gt, lt
  Comparator comparator_2 (.a(_1sec), .b(_3sec), .eq(comparator_2_eq));  // open: gt, lt
  Comparator comparator_3 (.a(_1sec), .b(_4sec), .eq(comparator_3_eq));  // open: gt, lt
  Comparator comparator_4 (.a(_2sec), .b(_1sec), .eq(comparator_4_eq));  // open: gt, lt
  Comparator comparator_5 (.a(_2sec), .b(_3sec), .eq(comparator_5_eq));  // open: gt, lt
  Comparator comparator_6 (.a(_2sec), .b(_4sec), .eq(comparator_6_eq));  // open: gt, lt
  Comparator comparator_7 (.a(_3sec), .b(_1sec), .eq(comparator_7_eq));  // open: gt, lt
  Comparator comparator_8 (.a(_3sec), .b(_2sec), .eq(comparator_8_eq));  // open: gt, lt
  Comparator comparator_9 (.a(_3sec), .b(_4sec), .eq(comparator_9_eq));  // open: gt, lt
  Comparator comparator_10 (.a(_4sec), .b(_1sec), .eq(comparator_10_eq));  // open: gt, lt
  Comparator comparator_11 (.a(_4sec), .b(_2sec), .eq(comparator_11_eq));  // open: gt, lt
  Comparator comparator_12 (.a(_4sec), .b(_3sec), .eq(comparator_12_eq));  // open: gt, lt
  or or_2 (or_2_out, comparator_1_eq, comparator_2_eq, comparator_3_eq, comparator_4_eq, comparator_5_eq, comparator_6_eq, comparator_7_eq, comparator_8_eq, comparator_9_eq, comparator_10_eq, comparator_11_eq, comparator_12_eq);
  // Probe on _1sec
  // Probe on _2sec
  // Probe on _3sec
  // Probe on _4sec

  // Other names for the same wires on the sheet: _1ch[7:0] = _1sec; _2ch[7:0] = _2sec; _3ch[7:0] = _3sec;
  //   _4ch[7:0] = _4sec
endmodule

module bcd (
  input  [7:0] attempt,
  output [7:0] attempt_2
);

  wire comparator_1_gt, comparator_2_lt;
  wire [7:0] adder_1_out, multiplexer_1_out, multiplexer_2_out;

  // Probe on attempt
  Comparator #(.mode("unsigned")) comparator_1 (.a(attempt), .b(8'h9), .gt(comparator_1_gt));  // open: eq, lt
  Multiplexer #(.width(8), .enable("false")) multiplexer_1 (
    .in0({8{1'b0}}), .in1(8'h6), .out(multiplexer_1_out), .sel(comparator_1_gt));
  // Probe on adder_1_out
  Adder adder_1 (.a(attempt), .b(multiplexer_1_out), .out(adder_1_out));  // open: cin, cout
  // Probe on adder_1_out[3:0]
  // Probe on adder_1_out
  Comparator #(.width(4), .mode("unsigned")) comparator_2 (
    .a(4'b1001), .b(adder_1_out[3:0]), .lt(comparator_2_lt));  // open: gt, eq
  Multiplexer #(.width(8), .enable("false")) multiplexer_2 (
    .in0({8{1'b0}}), .in1(8'h6), .out(multiplexer_2_out), .sel(comparator_2_lt));
  // Probe on attempt_2
  Adder adder_2 (.a(multiplexer_2_out), .b(adder_1_out), .out(attempt_2));  // open: cin, cout
endmodule

module block (
  input  knp,
  input  nv,
  input  nw,
  output signal
);

  wire d_ff_1_q, or_1_out;

  Multiplexer #(.enable("false")) multiplexer_1 (.in0(knp), .in1(1'b0), .out(signal), .sel(d_ff_1_q));
  D_Flip_Flop #(.trigger("falling")) d_ff_1 (
    .clk(knp), .D(1'b1), .Q(d_ff_1_q), .reset(or_1_out));  // open: Qn, preset, en
  or or_1 (or_1_out, nv, nw);
endmodule
